// Logisim project Circuit.circ as structural Verilog: 3 circuits, main circuit main
module main (
  input  in_1,
  input  in_2,
  input  in_3,
  input  in_4,
  input  in_5,
  input  in_6,
  input  in_7,
  input  in_8,
  output out_9,
  output out_10,
  output out_11,
  output out_12,
  output out_13,
  output out_14,
  output out_15,
  output out_16
);

  eightbit2compliment eightbit2compliment_1 (
    .I7(in_1), .I6(in_2), .I5(in_3), .I4(in_4), .I3(in_5), .I2(in_6), .I1(in_7), .I0(in_8), .O7(out_9),
    .O6(out_10), .O5(out_11), .O4(out_12), .O3(out_13), .O2(out_14), .O1(out_15), .O0(out_16));
endmodule

module eightbit2compliment (
  input  I7,
  input  I6,
  input  I5,
  input  I4,
  input  I3,
  input  I2,
  input  I1,
  input  I0,
  output O6,
  output O5,
  output O4,
  output O3,
  output O2,
  output O1,
  output O0,
  output O7
);

  wire adder_2_cout, adder_3_cout, adder_4_cout, adder_5_cout, adder_6_cout, adder_7_cout, adder_8_cout,
       not_1_out, not_2_out, not_3_out, not_4_out, not_5_out, not_6_out, not_7_out, not_8_out;

  not not_1 (not_1_out, I7);
  not not_2 (not_2_out, I6);
  Adder #(.width(1)) adder_1 (.a(not_1_out), .b(adder_2_cout), .out(O7));  // open: cin, cout
  not not_3 (not_3_out, I5);
  Adder #(.width(1)) adder_2 (.a(not_2_out), .b(adder_3_cout), .out(O6), .cout(adder_2_cout));  // open: cin
  not not_4 (not_4_out, I4);
  Adder #(.width(1)) adder_3 (.a(not_3_out), .b(adder_4_cout), .out(O5), .cout(adder_3_cout));  // open: cin
  not not_5 (not_5_out, I3);
  Adder #(.width(1)) adder_4 (.a(not_4_out), .b(adder_5_cout), .out(O4), .cout(adder_4_cout));  // open: cin
  not not_6 (not_6_out, I2);
  Adder #(.width(1)) adder_5 (.a(not_5_out), .b(adder_6_cout), .out(O3), .cout(adder_5_cout));  // open: cin
  not not_7 (not_7_out, I1);
  Adder #(.width(1)) adder_6 (.a(not_6_out), .b(adder_7_cout), .out(O2), .cout(adder_6_cout));  // open: cin
  not not_8 (not_8_out, I0);
  Adder #(.width(1)) adder_7 (.a(not_7_out), .b(adder_8_cout), .out(O1), .cout(adder_7_cout));  // open: cin
  Adder #(.width(1)) adder_8 (.a(not_8_out), .b(1'b1), .out(O0), .cout(adder_8_cout));  // open: cin
endmodule

module sixteenbit2compliment (
  input  in_1,
  input  in_2,
  input  in_3,
  input  in_4,
  input  in_5,
  input  in_6,
  input  in_7,
  input  in_8,
  input  in_9,
  input  in_10,
  input  in_11,
  input  in_12,
  input  in_13,
  input  in_14,
  input  in_15,
  input  in_16
);

  wire adder_1_cout, adder_1_out, adder_2_cout, adder_2_out, adder_3_cout, adder_3_out, adder_4_cout,
       adder_4_out, adder_5_cout, adder_5_out, adder_6_cout, adder_6_out, adder_7_cout, adder_7_out,
       adder_8_cout, adder_8_out, adder_9_cout, adder_9_out, adder_10_cout, adder_10_out, adder_11_cout,
       adder_11_out, adder_12_cout, adder_12_out, adder_13_cout, adder_13_out, adder_14_cout, adder_14_out,
       adder_15_cout, adder_15_out, adder_16_cout, adder_16_out, not_1_out, not_2_out, not_3_out, not_4_out,
       not_5_out, not_6_out, not_7_out, not_8_out, not_9_out, not_10_out, not_11_out, not_12_out, not_13_out,
       not_14_out, not_15_out, not_16_out;

  not not_1 (not_1_out, in_9);
  LED led_1 (.in(adder_1_out));
  not not_2 (not_2_out, in_10);
  Adder #(.width(1)) adder_1 (.a(not_1_out), .b(adder_2_cout), .out(adder_1_out), .cout(adder_1_cout));  // open: cin
  LED led_2 (.in(adder_1_cout));
  LED led_3 (.in(adder_2_out));
  not not_3 (not_3_out, in_11);
  Adder #(.width(1)) adder_2 (.a(not_2_out), .b(adder_3_cout), .out(adder_2_out), .cout(adder_2_cout));  // open: cin
  LED led_4 (.in(adder_3_out));
  not not_4 (not_4_out, in_12);
  Adder #(.width(1)) adder_3 (.a(not_3_out), .b(adder_4_cout), .out(adder_3_out), .cout(adder_3_cout));  // open: cin
  LED led_5 (.in(adder_4_out));
  not not_5 (not_5_out, in_13);
  Adder #(.width(1)) adder_4 (.a(not_4_out), .b(adder_5_cout), .out(adder_4_out), .cout(adder_4_cout));  // open: cin
  LED led_6 (.in(adder_5_out));
  not not_6 (not_6_out, in_14);
  Adder #(.width(1)) adder_5 (.a(not_5_out), .b(adder_6_cout), .out(adder_5_out), .cout(adder_5_cout));  // open: cin
  LED led_7 (.in(adder_6_out));
  not not_7 (not_7_out, in_15);
  Adder #(.width(1)) adder_6 (.a(not_6_out), .b(adder_7_cout), .out(adder_6_out), .cout(adder_6_cout));  // open: cin
  LED led_8 (.in(adder_7_out));
  Adder #(.width(1)) adder_7 (.a(not_7_out), .b(adder_8_cout), .out(adder_7_out), .cout(adder_7_cout));  // open: cin
  LED led_9 (.in(adder_8_out));
  not not_8 (not_8_out, in_16);
  Adder #(.width(1)) adder_8 (.a(not_8_out), .b(adder_9_cout), .out(adder_8_out), .cout(adder_8_cout));  // open: cin
  not not_9 (not_9_out, in_1);
  LED led_10 (.in(adder_9_out));
  not not_10 (not_10_out, in_2);
  Adder #(.width(1)) adder_9 (.a(not_9_out), .b(adder_10_cout), .out(adder_9_out), .cout(adder_9_cout));  // open: cin
  LED led_11 (.in(adder_10_out));
  not not_11 (not_11_out, in_3);
  Adder #(.width(1)) adder_10 (
    .a(not_10_out), .b(adder_11_cout), .out(adder_10_out), .cout(adder_10_cout));  // open: cin
  LED led_12 (.in(adder_11_out));
  not not_12 (not_12_out, in_4);
  Adder #(.width(1)) adder_11 (
    .a(not_11_out), .b(adder_12_cout), .out(adder_11_out), .cout(adder_11_cout));  // open: cin
  LED led_13 (.in(adder_12_out));
  not not_13 (not_13_out, in_5);
  Adder #(.width(1)) adder_12 (
    .a(not_12_out), .b(adder_13_cout), .out(adder_12_out), .cout(adder_12_cout));  // open: cin
  LED led_14 (.in(adder_13_out));
  not not_14 (not_14_out, in_6);
  Adder #(.width(1)) adder_13 (
    .a(not_13_out), .b(adder_14_cout), .out(adder_13_out), .cout(adder_13_cout));  // open: cin
  LED led_15 (.in(adder_14_out));
  not not_15 (not_15_out, in_7);
  Adder #(.width(1)) adder_14 (
    .a(not_14_out), .b(adder_15_cout), .out(adder_14_out), .cout(adder_14_cout));  // open: cin
  LED led_16 (.in(adder_15_out));
  Adder #(.width(1)) adder_15 (
    .a(not_15_out), .b(adder_16_cout), .out(adder_15_out), .cout(adder_15_cout));  // open: cin
  LED led_17 (.in(adder_16_out));
  not not_16 (not_16_out, in_8);
  Adder #(.width(1)) adder_16 (.a(not_16_out), .b(1'b1), .out(adder_16_out), .cout(adder_16_cout));  // open: cin
endmodule
